// Digital circuit programCounter.dig as structural Verilog
module programCounter (
  input  enable,
  input  clr,
  input  clk,
  output [7:0] out
);

  wire sixteenbitincrementer_1_p3;

  // sixteenBitIncrementer sixteenbitincrementer_1: pin names not known; wires that end beside it: out, 1'b1, sixteenbitincrementer_1_p3
  // sixteenBitReg sixteenbitreg_1: pin names not known; wires that end beside it: sixteenbitincrementer_1_p3, enable, clk, clr, out
endmodule
