// Digital circuit twoBitBusMux.dig as structural Verilog
module twoBitBusMux (
  input  [1:0] a,
  input  [1:0] b,
  input  sel,
  output [1:0] y
);

  twoBitMux twobitmux_1 (.in_a(a[0]), .in_b(b[0]), .sel(sel), .out(y[0]));
  twoBitMux twobitmux_2 (.in_a(a[1]), .in_b(b[1]), .sel(sel), .out(y[1]));
endmodule
