// Digital circuit addressGen.dig as structural Verilog
module addressGen (
  input  [15:0] data_in,
  input  clk,
  input  clr,
  input  use__pc,
  input  load__mar,
  output [15:0] addr_out
);

  wire not_1_out, pc;
  wire [15:0] mar;

  // programCounter programcounter_1: pin names not known; wires that end beside it: use__pc, clr, clk, pc
  sixteenBitReg sixteenbitreg_1 (.in(data_in), .sel(load__mar), .clr(clr), .clk(clk), .out(mar));
  not not_1 (not_1_out, use__pc);
  // sixteenBitMux sixteenbitmux_1: pin names not known; wires that end beside it: pc, mar, not_1_out, addr_out
endmodule
